# Fritzing sketch hand (saved by Fritzing 0.9.10b)
breadboards: 1

parts:
  Part1 = Arduino Nano (Rev3.0) (ICSP)
  Part2 = NRF24L01+ Breakout Board
  Part3 = InvenSense MPU6050
  R2 = Rotary Potentiometer (Small) [maximum_resistance=100kΩ knob_status=50% power=0.5W package=THT]
  Grove1 = Grove OLED 128x96  # not connected

nets:
  GND: Part1.GND, Part2.GND, Part3.GND, R2.leg1
  N1: Part1.D9, Part2.CE
  N2: Part1.D10, Part2.CS
  N3: Part1.D11/MOSI, Part2.MOSI
  N4: Part1.D12/MISO, Part2.MISO
  5V: Part1.5V, Part3.VCC, R2.leg2
  N5: Part1.A5, Part3.SCL
  N6: Part1.A4, Part3.SDA
  N7: Part1.A0, R2.wiper
  3V3: Part1.3V3, Part2.VCC
  N8: Part1.D13/SCK, Part2.SCK
